# Fritzing sketch prototypeLayoutSketch (saved by Fritzing 0.9.3b)
breadboards: 2

parts:
  S1 = Pushbutton [package="[THT]"]
  R1 = Resistor [tolerance=±5% resistance=1k package=THT]
  S2 = Pushbutton [package="[THT]"]
  R2 = Resistor [tolerance=±5% resistance=1k package=THT]
  Part1 = Arduino Mega ADK (Rev3)
  S3 = Pushbutton [package="[THT]"]
  R3 = Resistor [tolerance=±5% resistance=1k package=THT]
  S4 = Pushbutton [package="[THT]"]
  R4 = Resistor [tolerance=±5% resistance=1k package=THT]
  S5 = Pushbutton [package="[THT]"]
  R5 = Resistor [tolerance=±5% resistance=1k package=THT]
  S6 = Pushbutton [package="[THT]"]
  R6 = Resistor [tolerance=±5% resistance=1k package=THT]
  S7 = Pushbutton [package="[THT]"]
  R7 = Resistor [tolerance=±5% resistance=1k package=THT]
  S8 = Pushbutton [package="[THT]"]
  R8 = Resistor [tolerance=±5% resistance=1k package=THT]
  S9 = Pushbutton [package="[THT]"]
  S10 = Pushbutton [package="[THT]"]
  S11 = Pushbutton [package="[THT]"]
  S12 = Pushbutton [package="[THT]"]
  S13 = Pushbutton [package="[THT]"]
  S14 = Pushbutton [package="[THT]"]
  S15 = Pushbutton [package="[THT]"]
  S16 = Pushbutton [package="[THT]"]
  R9 = Resistor [tolerance=±5% resistance=1k package=THT]
  R10 = Resistor [tolerance=±5% resistance=1k package=THT]
  R11 = Resistor [tolerance=±5% resistance=1k package=THT]
  R12 = Resistor [tolerance=±5% resistance=1k package=THT]
  R13 = Resistor [tolerance=±5% resistance=1k package=THT]
  R14 = Resistor [tolerance=±5% resistance=1k package=THT]
  R15 = Resistor [tolerance=±5% resistance=1k package=THT]
  R16 = Resistor [tolerance=±5% resistance=1k package=THT]
  R17 = Resistor [tolerance=±5% resistance=470 package="2512 [SMD]"]
  Part2 = NeoPixel NeoMatrix 8x8 [part_number=1487]

nets:
  N1: S1.Pin_1, S1.Pin_2, R1.Pin_0, Part1.D35
  5V: S1.Pin_3, S1.Pin_4, S2.Pin_3, S2.Pin_4, Part1.5V, S3.Pin_3, S3.Pin_4, S4.Pin_3, S4.Pin_4, S5.Pin_3, S5.Pin_4, S6.Pin_3, S6.Pin_4, S7.Pin_3, S7.Pin_4, S8.Pin_3, S8.Pin_4, Part2.VDD
  GND: R1.Pin_1, R2.Pin_1, Part1.GND, R3.Pin_1, R4.Pin_1, R5.Pin_1, R6.Pin_1, R7.Pin_1, R8.Pin_1, Part2.GND
  N2: S2.Pin_1, S2.Pin_2, R2.Pin_0, Part1.D37
  N3: Part1.D3_PWM, R17.Pin_1
  N4: Part1.D22, S14.Pin_1, S14.Pin_2, R14.Pin_0
  N5: Part1.D23, S15.Pin_1, S15.Pin_2, R13.Pin_0
  N6: Part1.D24, S12.Pin_1, S12.Pin_2, R15.Pin_0
  N7: Part1.D25, S11.Pin_1, S11.Pin_2, R16.Pin_0
  N8: Part1.D27, S13.Pin_1, S13.Pin_2, R12.Pin_0
  N9: Part1.D29, S16.Pin_1, S16.Pin_2, R9.Pin_0
  N10: Part1.D31, S9.Pin_1, S9.Pin_2, R10.Pin_0
  N11: Part1.D33, S10.Pin_1, S10.Pin_2, R11.Pin_0
  N12: Part1.D39, S3.Pin_1, S3.Pin_2, R3.Pin_0
  N13: Part1.D41, S4.Pin_1, S4.Pin_2, R4.Pin_0
  N14: Part1.D43, S5.Pin_1, S5.Pin_2, R5.Pin_0
  N15: Part1.D45, S6.Pin_1, S6.Pin_2, R6.Pin_0
  N16: Part1.D47, S7.Pin_1, S7.Pin_2, R7.Pin_0
  N17: Part1.D49, S8.Pin_1, S8.Pin_2, R8.Pin_0
  N18: S9.Pin_3, S9.Pin_4, S10.Pin_3, S10.Pin_4, S11.Pin_3, S11.Pin_4, S12.Pin_3, S12.Pin_4, S13.Pin_3, S13.Pin_4, S14.Pin_3, S14.Pin_4, S15.Pin_3, S15.Pin_4, S16.Pin_3, S16.Pin_4
  N19: R9.Pin_1, R10.Pin_1, R11.Pin_1, R12.Pin_1, R13.Pin_1, R14.Pin_1, R15.Pin_1, R16.Pin_1
  N20: R17.Pin_0, Part2.IN

custom parts:
  NeoPixel NeoMatrix 8x8: Put on your sunglasses before wiring up this LED matrix - 64 eye-blistering RGB LEDs adorn the NeoMatrix for a blast of configurable color. Arranged in an 8x8 matrix, each pixel is individually addressable. Only one microcontroller pin is required to control all the LEDs, and you get 24 bit color for each LED.
